# Fritzing sketch AutoPlantPrototyping (saved by Fritzing 0.9.3b)
breadboards: 1

parts:
  Rasberry_Pi_Zero_W = Raspberry Pi Zero  # not connected
  I2C = female pin header, 4 pins [form="♀ (female)"]  # not connected
  Grove_Serial = female pin header, 4 pins [form="♀ (female)"]  # not connected
  D13/16 = female pin header, 4 pins [form="♀ (female)"]  # not connected
  D4/5 = female pin header, 4 pins [form="♀ (female)"]  # not connected
  I2C_2 = female pin header, 4 pins [form="♀ (female)"]  # not connected
  I2C_3 = female pin header, 4 pins [form="♀ (female)"]
  I2C_4 = female pin header, 4 pins [form="♀ (female)"]
  D21/26 = female pin header, 4 pins [form="♀ (female)"]  # not connected
  D26 = female pin header, 4 pins [form="♀ (female)"]  # not connected
  D16/19 = female pin header, 4 pins [form="♀ (female)"]  # not connected
  D19/20 = female pin header, 4 pins [form="♀ (female)"]  # not connected
  D20/21 = female pin header, 4 pins [form="♀ (female)"]  # not connected
  D5/6 = female pin header, 4 pins [form="♀ (female)"]  # not connected
  D6/12 = female pin header, 4 pins [form="♀ (female)"]  # not connected
  D12/13 = female pin header, 4 pins [form="♀ (female)"]  # not connected
  5_5_BARREL_JACK_1 = 2.1mm Barrel Jack with Terminal Block
  5_5_BARREL_JACK_2 = 2.1mm Barrel Jack with Terminal Block
  Relay_Module = 16-Channel Relay Module [package=relay-16ch]
  Soil_Moisture_Sensor_2 = Soil Moisture Sensor
  Soil_Moisture_Sensor_3 = Soil Moisture Sensor
  Soil_Moisture_Sensor_1 = Soil Moisture Sensor
  Soil_Moisture_Sensor_4 = Soil Moisture Sensor
  12V_DC_Motor = DC Motor
  Fan = DC Motor
  Micro-USB_Cable = USB_MICROB_PLUG [package=micro-b-ra-th]
  I2C_5 = female pin header, 4 pins [form="♀ (female)"]
  A1 = female pin header, 4 pins [form="♀ (female)"]
  A3 = female pin header, 4 pins [form="♀ (female)"]
  A0 = female pin header, 4 pins [form="♀ (female)"]
  A2 = female pin header, 4 pins [form="♀ (female)"]
  120v_AC_Wall_Outlet = female pin header, 3 pins [form="♀ (female)"]
  120v_AC_Wall_Outlet_2 = female pin header, 3 pins [form="♀ (female)"]
  J1 = Raspberry Pi Header 40pin [package=THT]
  J2 = female pin header, 2 pins [form="♀ (female)"]
  J3 = female pin header, 2 pins [form="♀ (female)"]
  BAT1 = BC9VPC [package=bc9vpc]
  Temp/Humidity_Sensor = Adafruit Si7021 Temp Humidity
  Light_Sensor = Photocell (LDR) [package=THT]
  part = Ceramic Capacitor [capacitance=0.1µF voltage=6.3V package="200 mil [THT, multilayer]"]

nets:
  N1: I2C_3.pin1, Temp/Humidity_Sensor.GND
  N2: I2C_3.pin2, Temp/Humidity_Sensor.VIN
  N3: I2C_3.pin3, Temp/Humidity_Sensor.SDA
  N4: I2C_3.pin4, Temp/Humidity_Sensor.SCL
  N5: I2C_4.pin1, I2C_5.pin1
  N6: I2C_4.pin2, I2C_5.pin2
  N7: I2C_4.pin3, I2C_5.pin3
  N8: I2C_4.pin4, I2C_5.pin4
  N9: 5_5_BARREL_JACK_1.POS, Relay_Module.K4_NO, 120v_AC_Wall_Outlet_2.pin3
  N10: 5_5_BARREL_JACK_1.NEG, 120v_AC_Wall_Outlet_2.pin2, J2.pin2
  N11: 5_5_BARREL_JACK_2.POS, Relay_Module.K1_NO, BAT1.V+
  N12: 5_5_BARREL_JACK_2.NEG, 12V_DC_Motor.pin_1, J3.pin2, BAT1.V-
  N13: Relay_Module.IN1, J1.IO23
  N14: Relay_Module.IN2, J1.IO24
  N15: Relay_Module.IN3, J1.IO22#12
  N16: Relay_Module.IN4, J1.IO22#14
  N17: Relay_Module.VCCOUT_5V, J1.3V3, Light_Sensor.pin_0
  N18: Relay_Module.OUT_GND, J1.GND, part.1
  N19: Relay_Module.K1_COM, 12V_DC_Motor.pin_2, J3.pin1
  N20: Relay_Module.K4_COM, Fan.pin_2, J2.pin1
  N21: Soil_Moisture_Sensor_2.SIG, A1.pin4
  N22: Soil_Moisture_Sensor_2.GND, A1.pin1
  N23: Soil_Moisture_Sensor_2.VCC, A1.pin2
  N24: Soil_Moisture_Sensor_3.SIG, A2.pin4
  N25: Soil_Moisture_Sensor_3.GND, A2.pin1
  N26: Soil_Moisture_Sensor_3.VCC, A2.pin2
  N27: Soil_Moisture_Sensor_1.SIG, A0.pin4
  N28: Soil_Moisture_Sensor_1.GND, A0.pin1
  N29: Soil_Moisture_Sensor_1.VCC, A0.pin2
  N30: Soil_Moisture_Sensor_4.SIG, A3.pin4
  N31: Soil_Moisture_Sensor_4.GND, A3.pin1
  N32: Soil_Moisture_Sensor_4.VCC, A3.pin2
  N33: Micro-USB_Cable.VCC, 120v_AC_Wall_Outlet.pin3
  N34: Micro-USB_Cable.D-, 120v_AC_Wall_Outlet.pin2
  N35: Micro-USB_Cable.D+, 120v_AC_Wall_Outlet.pin1
  N36: J1.IO4, Light_Sensor.pin_1, part.0

notes:
  Grove Interface HAT
  Grove ADC
  4 Channel Relay Module
  1uF

custom parts:
  16-Channel Relay Module: 16 channel relay module
  Raspberry Pi Header 40pin: Raspberry Pi 40 pin header - for creating your own shields. (Mar 2020, bb: make breadboard friendly (.4in pin spacing) and add labels. Schematic add labels. PCB make oblong pins to allow routing traces between the pins.)
  Adafruit Si7021 Temp Humidity: It's summer and you're sweating and your hair's all frizzy and all you really want to know is why the weatherman said this morning that today's relative humidity would max out at a perfectly reasonable 42% when it feels more like 77%. Enter the Si7021 Temperature + Humidity Sensor - the best way to prove the weatherman wrong! This lovely sensor for Silicon labs has ± 3% relative humidity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
