# Fritzing sketch SoilMoistureSensorADCpi (saved by Fritzing 0.9.3b)
breadboards: 1

parts:
  MCU1 = Raspberry Pi Zero
  Part3 = Adafruit ADS1115 16Bit I2C ADC [part_number="Adafruit #1085"]
  Part4 = Soil Moisture Sensor

nets:
  VDD: MCU1.pin_1, MCU1.pin_17, Part3.VDD, Part4.VCC
  N1: MCU1.pin_3, Part3.SDA
  N2: MCU1.pin_5, Part3.SCL
  GND: MCU1.pin_6, MCU1.pin_39, Part3.GND, Part4.GND
  N3: Part3.AIN0, Part4.SIG

custom parts:
  Adafruit ADS1115 16Bit I2C ADC: For microcontrollers without an analog-to-digital converter or when you want a higher-precision ADC, the ADS1115 provides 16-bit precision at 860 samples/second over I2C. The chip can be configured as 4 single-ended input channels, or two differential channels. As a nice bonus, it even includes a programmable gain amplifier, up to x16, to help boost up smaller single/differential signals to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
